// Logisim project EXERCICIO BLOG CIRCUITOS.circ as structural Verilog: 2 circuits, main circuit main
module main (
  input  A,
  input  B,
  input  C,
  input  D
);

  wire n7_seg_1_a_2, n7_seg_1_b_2, n7_seg_1_c_2, n7_seg_1_d_2, n7_seg_1_e, n7_seg_1_f, n7_seg_1_g;

  _7_seg u_7_seg_1 (
    .a_2(n7_seg_1_a_2), .b_2(n7_seg_1_b_2), .c_2(n7_seg_1_c_2), .d_2(n7_seg_1_d_2), .e(n7_seg_1_e),
    .f(n7_seg_1_f), .g(n7_seg_1_g), .A(A), .B(B), .C(C), .D(D));
  _7_Segment_Display u_7_segment_display_1 (
    .g(n7_seg_1_g), .f(n7_seg_1_f), .a(n7_seg_1_a_2), .b(n7_seg_1_b_2), .e(n7_seg_1_e), .d(n7_seg_1_d_2),
    .c(n7_seg_1_c_2));  // open: dp
endmodule

module _7_seg (
  input  A,
  input  B,
  input  C,
  input  D,
  output a_2,
  output b_2,
  output c_2,
  output d_2,
  output e,
  output f,
  output g
);

  wire and_1_out, and_2_out, and_3_out, and_4_out, and_5_out, and_6_out, and_7_out, and_8_out, and_9_out,
       and_10_out, and_11_out, and_12_out, not_1_out, not_2_out, xnor_1_out, xnor_2_out;

  not not_1 (not_1_out, B);
  not not_2 (not_2_out, C);
  or or_1 (c_2, B, not_2_out, D);
  and and_1 (and_1_out, ~B, ~D);  // AND_Gate
  and and_2 (and_2_out, ~B, C);  // AND_Gate
  and and_3 (and_3_out, C, ~D);  // AND_Gate
  and and_4 (and_4_out, B, ~C, D);  // AND_Gate
  and and_5 (and_5_out, ~B, ~D);  // AND_Gate
  buf and_6 (and_6_out, ~D);  // AND_Gate AND_Gate
  and and_7 (and_7_out, ~C, ~D);  // AND_Gate
  and and_8 (and_8_out, B, ~C);  // AND_Gate
  and and_9 (and_9_out, B, ~D);  // AND_Gate
  and and_10 (and_10_out, B, ~C);  // AND_Gate
  and and_11 (and_11_out, ~B, C);  // AND_Gate
  and and_12 (and_12_out, C, ~D);  // AND_Gate
  xnor xnor_1 (xnor_1_out, B, D);
  xnor xnor_2 (xnor_2_out, C, D);
  or or_2 (a_2, xnor_1_out, C, A);
  or or_3 (b_2, xnor_2_out, not_1_out);
  or or_4 (e, and_5_out, and_6_out);
  or or_5 (g, A, and_10_out, and_11_out, and_12_out);
  or or_6 (d_2, A, and_1_out, and_2_out, and_3_out, and_4_out);
  or or_7 (f, A, and_7_out, and_8_out, and_9_out);
endmodule
